// Logisim project RAM.circ as structural Verilog: 1 circuit, main circuit RAM
module RAM (
  input  [15:0] Addr,
  input  Reset,
  input  [15:0] Din,
  input  Write,
  input  CK,
  output [15:0] Dout
);

  wire nand_1_out, not_1_out, not_2_out;

  assign Dout = not_1_out ? Din : 16'bz;  // Controlled_Buffer controlled_buffer_1
  not not_1 (not_1_out, nand_1_out);
  not not_2 (not_2_out, CK);
  nand nand_1 (nand_1_out, not_2_out, Write);
  RAM_part #(.addrWidth(16), .dataWidth(16), .bus("asynch")) ram_1 (
    .addr(Addr), .data(Dout), .ld(nand_1_out), .clr(Reset));  // open: sel
endmodule
