// Logisim project controlunit.circ as structural Verilog: 1 circuit, main circuit Control Unit
module Control_Unit (
  input  [3:0] opcode,
  input  [2:0] fn,
  output MemWr,
  output Mem2Reg,
  output Immx2,
  output SignExt,
  output ALUSrc,
  output RegWr,
  output RegDst,
  output [1:0] PCSrc,
  output [2:0] ALUCtr
);

  wire nor_1_out;
  wire [2:0] rom_2_data, rom_3_data;

  nor nor_1 (nor_1_out, opcode[0], opcode[1], opcode[2], opcode[3]);
  ROM #(.addrWidth(4)) rom_1 (
    .addr(opcode), .data({PCSrc, RegDst, RegWr, ALUSrc, Immx2, Mem2Reg, MemWr}));  // open: sel
  ROM #(.addrWidth(4), .dataWidth(3)) rom_2 (.addr(opcode), .data(rom_2_data));  // open: sel
  ROM #(.addrWidth(3), .dataWidth(3)) rom_3 (.addr(fn), .data(rom_3_data));  // open: sel
  Multiplexer #(.width(3), .enable("false")) multiplexer_1 (
    .in0(rom_2_data), .in1(rom_3_data), .out(ALUCtr), .sel(nor_1_out));

  assign SignExt = Immx2;

  // Notes on the sheet:
  //   contents of rom_1 (hex, n*v repeats v):
  //   30 40 0 80 1e d 4*0 18 18
  //   contents of rom_2 (hex, n*v repeats v):
  //   0 3 0 0 2 2 4*0 2 3
  //   contents of rom_3 (hex, n*v repeats v):
  //   0 1 2 6
endmodule
