// Logisim project pcupdate.circ as structural Verilog: 1 circuit, main circuit PC Update
module PC_Update (
  input  [15:0] PCin,
  input  [5:0] imm,
  input  [11:0] addr,
  input  [1:0] PCSrc,
  output [15:0] PCOut
);

  wire [15:0] adder_1_out, adder_2_out, adder_3_out, se6_1_out_3, se12_1_out_3, x2_1_out_3, x2_2_out_3;

  se6 se6_1 (.in_1(imm), .SignExt(1'b1), .out_3(se6_1_out_3));
  se12 se12_1 (.in_1(addr), .SignExt(1'b1), .out_3(se12_1_out_3));
  Adder #(.width(16)) adder_1 (.a(16'h2), .b(PCin), .out(adder_1_out));  // open: cin, cout
  x2 x2_1 (.In(se6_1_out_3), .Immx2(1'b1), .out_3(x2_1_out_3));
  x2 x2_2 (.In(se12_1_out_3), .Immx2(1'b1), .out_3(x2_2_out_3));
  Adder #(.width(16)) adder_2 (.a(adder_1_out), .b(x2_1_out_3), .out(adder_2_out));  // open: cin, cout
  Adder #(.width(16)) adder_3 (.a(adder_1_out), .b(x2_2_out_3), .out(adder_3_out));  // open: cin, cout
  Multiplexer #(.select(2), .width(16), .enable("false")) multiplexer_1 (
    .in0(adder_1_out), .in1(adder_2_out), .in2(adder_3_out), .out(PCOut), .sel(PCSrc));  // open: in3
endmodule
