// Logisim project regfile.circ as structural Verilog: 1 circuit, main circuit register file
module register_file (
  input  [2:0] ReadAddr1,
  input  RegWr,
  input  [2:0] ReadAddr2,
  input  CK,
  input  [15:0] Data,
  input  [2:0] WriteAddr,
  input  Reset,
  output [15:0] D1,
  output [15:0] D2
);

  wire and_1_out, and_2_out, and_3_out, and_4_out, and_5_out, and_6_out, and_7_out, and_8_out,
       decoder_1_out0, decoder_1_out1, decoder_1_out2, decoder_1_out3, decoder_1_out4, decoder_1_out5,
       decoder_1_out6, decoder_1_out7, not_1_out;
  wire [15:0] R0_q, R1_q, R2_q, R3_q, R4_q, R5_q, R6_q, R7_q;

  Decoder #(.select(3), .enable("false")) decoder_1 (
    .out0(decoder_1_out0), .out1(decoder_1_out1), .out2(decoder_1_out2), .out3(decoder_1_out3),
    .out4(decoder_1_out4), .out5(decoder_1_out5), .out6(decoder_1_out6), .out7(decoder_1_out7),
    .sel(WriteAddr));
  not not_1 (not_1_out, CK);
  and and_1 (and_1_out, RegWr, decoder_1_out0);
  and and_2 (and_2_out, RegWr, decoder_1_out1);
  and and_3 (and_3_out, RegWr, decoder_1_out2);
  and and_4 (and_4_out, RegWr, decoder_1_out3);
  and and_5 (and_5_out, RegWr, decoder_1_out4);
  and and_6 (and_6_out, RegWr, decoder_1_out5);
  and and_7 (and_7_out, RegWr, decoder_1_out6);
  and and_8 (and_8_out, RegWr, decoder_1_out7);
  Register #(.width(16), .trigger("high")) R0 (.D(Data), .en(and_1_out), .Q(R0_q), .clk(not_1_out), .clr(Reset));
  Register #(.width(16), .trigger("high")) R1 (.D(Data), .en(and_2_out), .Q(R1_q), .clk(not_1_out), .clr(Reset));
  Register #(.width(16), .trigger("high")) R2 (.D(Data), .en(and_3_out), .Q(R2_q), .clk(not_1_out), .clr(Reset));
  Register #(.width(16), .trigger("high")) R3 (.D(Data), .en(and_4_out), .Q(R3_q), .clk(not_1_out), .clr(Reset));
  Register #(.width(16), .trigger("high")) R4 (.D(Data), .en(and_5_out), .Q(R4_q), .clk(not_1_out), .clr(Reset));
  Register #(.width(16), .trigger("high")) R5 (.D(Data), .en(and_6_out), .Q(R5_q), .clk(not_1_out), .clr(Reset));
  Register #(.width(16), .trigger("high")) R6 (.D(Data), .en(and_7_out), .Q(R6_q), .clk(not_1_out), .clr(Reset));
  Register #(.width(16), .trigger("high")) R7 (.D(Data), .en(and_8_out), .Q(R7_q), .clk(not_1_out), .clr(Reset));
  Multiplexer #(.select(3), .width(16)) multiplexer_1 (
    .in0(R0_q), .in1(R1_q), .in2(R2_q), .in3(R3_q), .in4(R4_q), .in5(R5_q), .in6(R6_q), .in7(R7_q), .out(D1),
    .sel(ReadAddr1));  // open: en
  Multiplexer #(.select(3), .width(16)) multiplexer_2 (
    .in0(R0_q), .in1(R1_q), .in2(R2_q), .in3(R3_q), .in4(R4_q), .in5(R5_q), .in6(R6_q), .in7(R7_q), .out(D2),
    .sel(ReadAddr2));  // open: en
endmodule
