// Logisim project se12.circ as structural Verilog: 1 circuit, main circuit se12
module se12 (
  input  [11:0] in_1,
  input  SignExt,
  output [15:0] out_3
);

  and and_1 (out_3[15], in_1[11], SignExt);

  assign out_3[14:0] = {{3{out_3[15]}}, in_1};
endmodule
