// Logisim project se6.circ as structural Verilog: 1 circuit, main circuit se6
module se6 (
  input  [5:0] in_1,
  input  SignExt,
  output [15:0] out_3
);

  and and_1 (out_3[15], in_1[5], SignExt);

  assign out_3[14:0] = {{9{out_3[15]}}, in_1};
endmodule
