// Logisim project x2.circ as structural Verilog: 1 circuit, main circuit x2
module x2 (
  input  [15:0] In,
  input  Immx2,
  output [15:0] out_3
);

  Multiplexer #(.width(16), .enable("false")) multiplexer_1 (
    .in0(In), .in1({In[14:0], 1'b0}), .out(out_3), .sel(Immx2));
endmodule
