// Logisim project zero.circ as structural Verilog: 1 circuit, main circuit zero
module zero (
  input  [15:0] In,
  output Zero
);

  nor nor_1 (Zero, In[0], In[1], In[2], In[3], In[4], In[5], In[6], In[7], In[8], In[9], In[10], In[11], In[12], In[13], In[14], In[15]);
endmodule
