// Logisim project 컴구프로젝트 1번문제.circ as structural Verilog: 1 circuit, main circuit main
module main (
  input  PCWr,
  input  reset
);

  wire ALUSrc, CK_out, immx2, Mem2Reg, MemWr, RegDst, RegWr, SignExt;
  wire [1:0] PCSrc;
  wire [2:0] ALUCtr, fn, multiplexer_1_out;
  wire [3:0] opcode;
  wire [11:3] rom_1_data;
  wire [15:0] alu_1_out_4, multiplexer_2_out, multiplexer_3_out, pc_update_1_pcout, ram_1_dout, register_1_q,
       Register_file_d1, Register_file_d2, se6_1_out_3, x2_1_out_3;

  PC_Update pc_update_1 (
    .PCin(register_1_q), .imm({rom_1_data[5:3], fn}), .addr({rom_1_data, fn}), .PCSrc(PCSrc),
    .PCOut(pc_update_1_pcout));
  Register #(.width(16)) register_1 (.D(pc_update_1_pcout), .en(PCWr), .Q(register_1_q), .clk(CK_out), .clr(reset));
  Clock CK (.out(CK_out));
  ROM #(.addrWidth(16), .dataWidth(16)) rom_1 (.addr(register_1_q), .data({opcode, rom_1_data, fn}));  // open: sel
  Control_Unit control_unit_1 (
    .opcode(opcode), .fn(fn), .MemWr(MemWr), .Mem2Reg(Mem2Reg), .Immx2(immx2), .SignExt(SignExt),
    .ALUSrc(ALUSrc), .RegWr(RegWr), .RegDst(RegDst), .PCSrc(PCSrc), .ALUCtr(ALUCtr));
  Multiplexer #(.width(3)) multiplexer_1 (
    .in0(rom_1_data[8:6]), .in1(rom_1_data[5:3]), .out(multiplexer_1_out), .sel(RegDst));  // open: en
  se6 se6_1 (.in_1({rom_1_data[5:3], fn}), .SignExt(RegDst), .out_3(se6_1_out_3));
  register_file Register_file (
    .ReadAddr1(rom_1_data[11:9]), .RegWr(RegWr), .ReadAddr2(rom_1_data[8:6]), .CK(CK_out),
    .Data(multiplexer_3_out), .WriteAddr(multiplexer_1_out), .Reset(reset), .D1(Register_file_d1),
    .D2(Register_file_d2));
  x2 x2_1 (.In(se6_1_out_3), .Immx2(immx2), .out_3(x2_1_out_3));
  Multiplexer #(.width(16)) multiplexer_2 (
    .in0(Register_file_d2), .in1(x2_1_out_3), .out(multiplexer_2_out), .sel(ALUSrc));  // open: en
  Multiplexer #(.width(16)) multiplexer_3 (
    .in0(alu_1_out_4), .in1(ram_1_dout), .out(multiplexer_3_out), .sel(Mem2Reg));  // open: en
  ALU alu_1 (.Ctr(ALUCtr), .A(Register_file_d1), .B(multiplexer_2_out), .out_4(alu_1_out_4));
  RAM ram_1 (.Addr(alu_1_out_4), .Reset(reset), .Din(Register_file_d2), .Write(MemWr), .CK(CK_out), .Dout(ram_1_dout));
endmodule
