// Logisim project 3주차과제_1_201921009_엄지호.circ as structural Verilog: 1 circuit, main circuit main
module main (
  input  X,
  input  Y,
  input  X_2,
  input  Y_2,
  input  a,
  input  X_3,
  input  Y_3,
  input  b,
  input  X_4,
  input  Y_4,
  input  c,
  input  X_5,
  input  Y_5,
  input  d,
  input  X_6,
  input  Y_6,
  output out_17,
  output out_18
);

  wire and_1_out, and_2_out, and_3_out, and_4_out, and_5_out, and_6_out, not_1_out, not_2_out, not_3_out,
       not_4_out, not_5_out, not_6_out, or_1_out, or_2_out, undriven;

  not not_1 (not_1_out, X_3);
  not not_2 (not_2_out, Y_3);
  not not_3 (not_3_out, Y_4);
  not not_4 (not_4_out, c);
  not not_5 (not_5_out, X);
  not not_6 (not_6_out, Y_2);
  and and_1 (and_1_out, not_5_out, Y);
  and and_2 (and_2_out, X_2, not_6_out);
  and and_3 (and_3_out, undriven, not_1_out, not_2_out);
  and and_4 (and_4_out, b, X_4, not_3_out);
  and and_5 (and_5_out, not_4_out, not_4_out, X_5, Y_5, Y_5);
  and and_6 (and_6_out, d, d, X_6, Y_6);
  or or_1 (or_1_out, and_3_out, and_4_out);
  or or_2 (or_2_out, and_5_out, and_6_out);
  or or_3 (out_17, and_1_out, and_2_out);
  or or_4 (out_18, or_1_out, or_2_out);
endmodule
