// Logisim project 3주차과제_2_201921009_엄지호.circ as structural Verilog: 1 circuit, main circuit main
module main (
  input  a,
  input  b,
  input  a_2,
  input  b_2,
  input  c,
  output out_6
);

  wire and_1_out, and_2_out, xor_1_out;

  and and_1 (and_1_out, a, b);
  xor xor_1 (xor_1_out, a_2, b_2);
  and and_2 (and_2_out, xor_1_out, c);
  or or_1 (out_6, and_1_out, and_2_out);
endmodule
