// Logisim project 4주차과제_2_201921009_엄지호.circ as structural Verilog: 1 circuit, main circuit main
module main (
  input  A2,
  input  A0,
  input  B2,
  input  B0,
  input  Cin,
  input  A3,
  input  B3,
  input  A1,
  input  B1,
  output S2,
  output S0,
  output S3,
  output S1,
  output Cout_3
);

  wire and_1_out, and_2_out, and_3_out, and_4_out, and_5_out, and_6_out, and_7_out, and_8_out, or_1_out,
       or_2_out, or_3_out, xor_1_out, xor_2_out, xor_5_out, xor_6_out;

  xor xor_1 (xor_1_out, A0, B0);
  and and_1 (and_1_out, A0, B0);
  xor xor_2 (xor_2_out, A1, B1);
  and and_2 (and_2_out, A1, B1);
  xor xor_3 (S0, xor_1_out, Cin);
  and and_3 (and_3_out, xor_1_out, Cin);
  or or_1 (or_1_out, and_3_out, and_1_out);
  xor xor_4 (S1, xor_2_out, or_1_out);
  and and_4 (and_4_out, xor_2_out, or_1_out);
  or or_2 (or_2_out, and_4_out, and_2_out);
  xor xor_5 (xor_5_out, A2, B2);
  and and_5 (and_5_out, A2, B2);
  xor xor_6 (xor_6_out, A3, B3);
  and and_6 (and_6_out, A3, B3);
  and and_7 (and_7_out, xor_5_out, or_2_out);
  xor xor_7 (S2, xor_5_out, or_2_out);
  or or_3 (or_3_out, and_7_out, and_5_out);
  and and_8 (and_8_out, xor_6_out, or_3_out);
  xor xor_8 (S3, xor_6_out, or_3_out);
  or or_4 (Cout_3, and_8_out, and_6_out);

  // Notes on the sheet:
  //   Cout 0
  //   Cout 1
  //   Cout 2
endmodule
