// Logisim project 5주차과제_4_201921009_엄지호.circ as structural Verilog: 1 circuit, main circuit main
module main (
  input  [1:0] width,
  input  Shift_In,
  output Shfit_Out
);

  wire clock_1_out, d_ff_1_q, d_ff_2_q, d_ff_3_q, d_ff_4_q, d_ff_5_q, d_ff_6_q, d_ff_7_q, multiplexer_1_out,
       multiplexer_2_out, multiplexer_3_out, multiplexer_4_out, multiplexer_5_out, multiplexer_6_out,
       multiplexer_7_out, multiplexer_8_out;

  Clock clock_1 (.out(clock_1_out));
  Multiplexer #(.select(2)) multiplexer_1 (
    .in1(Shift_In), .in2(Shift_In), .in3(Shift_In), .out(multiplexer_1_out), .sel(width));  // open: in0, en
  D_Flip_Flop d_ff_1 (.clk(clock_1_out), .D(multiplexer_1_out), .Q(d_ff_1_q));  // open: Qn, preset, en, reset
  Multiplexer #(.select(2)) multiplexer_2 (
    .in1(d_ff_1_q), .in2(multiplexer_1_out), .in3(multiplexer_1_out), .out(multiplexer_2_out), .sel(width));  // open: in0, en
  D_Flip_Flop d_ff_2 (.clk(clock_1_out), .D(multiplexer_2_out), .Q(d_ff_2_q));  // open: Qn, preset, en, reset
  Multiplexer #(.select(2)) multiplexer_3 (
    .in1(d_ff_2_q), .in2(d_ff_2_q), .in3(multiplexer_2_out), .out(multiplexer_3_out), .sel(width));  // open: in0, en
  D_Flip_Flop d_ff_3 (.clk(clock_1_out), .D(multiplexer_3_out), .Q(d_ff_3_q));  // open: Qn, preset, en, reset
  Multiplexer #(.select(2)) multiplexer_4 (
    .in1(d_ff_3_q), .in2(multiplexer_3_out), .in3(d_ff_3_q), .out(multiplexer_4_out), .sel(width));  // open: in0, en
  D_Flip_Flop d_ff_4 (.clk(clock_1_out), .D(multiplexer_4_out), .Q(d_ff_4_q));  // open: Qn, preset, en, reset
  Multiplexer #(.select(2)) multiplexer_5 (
    .in1(d_ff_4_q), .in2(d_ff_4_q), .in3(multiplexer_4_out), .out(multiplexer_5_out), .sel(width));  // open: in0, en
  D_Flip_Flop d_ff_5 (.clk(clock_1_out), .D(multiplexer_5_out), .Q(d_ff_5_q));  // open: Qn, preset, en, reset
  Multiplexer #(.select(2)) multiplexer_6 (
    .in1(d_ff_5_q), .in2(multiplexer_5_out), .in3(multiplexer_5_out), .out(multiplexer_6_out), .sel(width));  // open: in0, en
  D_Flip_Flop d_ff_6 (.clk(clock_1_out), .D(multiplexer_6_out), .Q(d_ff_6_q));  // open: Qn, preset, en, reset
  Multiplexer #(.select(2)) multiplexer_7 (
    .in1(d_ff_6_q), .in2(d_ff_6_q), .in3(d_ff_6_q), .out(multiplexer_7_out), .sel(width));  // open: in0, en
  D_Flip_Flop d_ff_7 (.clk(clock_1_out), .D(multiplexer_7_out), .Q(d_ff_7_q));  // open: Qn, preset, en, reset
  Multiplexer #(.select(2)) multiplexer_8 (
    .in1(d_ff_7_q), .in2(multiplexer_7_out), .in3(multiplexer_7_out), .out(multiplexer_8_out), .sel(width));  // open: in0, en
  D_Flip_Flop d_ff_8 (.clk(clock_1_out), .D(multiplexer_8_out), .Q(Shfit_Out));  // open: Qn, preset, en, reset
endmodule
