// Logisim project 7주차과제_201921009_엄지호.circ as structural Verilog: 1 circuit, main circuit main
module main (
  input  X,
  output out_2
);

  wire and_1_out, and_2_out, and_3_out, and_4_out, and_5_out, and_6_out, and_7_out, and_8_out, clock_1_out,
       not_1_out, not_2_out, not_3_out, not_4_out, not_5_out, not_6_out, not_7_out, or_1_out, or_2_out, Q0_q,
       Q1_q, Q2_q, xor_1_out, xor_2_out;

  not not_1 (not_1_out, Q2_q);
  and and_1 (and_1_out, X, not_1_out);
  not not_2 (not_2_out, Q1_q);
  and and_2 (and_2_out, Q0_q, X);
  and and_3 (and_3_out, Q2_q, not_2_out, X);
  xor xor_1 (xor_1_out, Q0_q, Q1_q);
  and and_4 (and_4_out, xor_1_out, and_1_out);
  xor xor_2 (xor_2_out, Q1_q, Q2_q);
  or or_1 (or_1_out, and_5_out, and_3_out);
  Clock clock_1 (.out(clock_1_out));
  and and_5 (and_5_out, xor_2_out, and_2_out);
  D_Flip_Flop Q0 (.clk(clock_1_out), .D(or_2_out), .Q(Q0_q));  // open: Qn, preset, en, reset
  D_Flip_Flop Q1 (.clk(clock_1_out), .D(and_4_out), .Q(Q1_q));  // open: Qn, preset, en, reset
  D_Flip_Flop Q2 (.clk(clock_1_out), .D(or_1_out), .Q(Q2_q));  // open: Qn, preset, en, reset
  not not_3 (not_3_out, Q0_q);
  not not_4 (not_4_out, Q1_q);
  not not_5 (not_5_out, Q2_q);
  and and_6 (and_6_out, not_3_out, X, not_4_out);
  and and_7 (and_7_out, not_3_out, not_5_out);
  not not_6 (not_6_out, Q1_q);
  not not_7 (not_7_out, Q1_q);
  and and_8 (and_8_out, Q2_q, not_6_out);
  or or_2 (or_2_out, and_6_out, and_7_out, and_8_out);
  and and_9 (out_2, Q0_q, not_7_out, Q2_q);
endmodule
