// Logisim project 4bitadder.circ as structural Verilog: 1 circuit, main circuit main
module main (
  input  [3:0] A_3_0,
  input  [3:0] B_3_0,
  input  Cin,
  output Cout,
  output [3:0] S_3_0
);

  wire main_2_cout, main_3_cout, main_4_cout;

  fulladder_main main_1 (.A(A_3_0[3]), .B(B_3_0[3]), .Cin(main_2_cout), .S(S_3_0[3]), .Cout(Cout));
  fulladder_main main_2 (.A(A_3_0[2]), .B(B_3_0[2]), .Cin(main_3_cout), .S(S_3_0[2]), .Cout(main_2_cout));
  fulladder_main main_3 (.A(A_3_0[1]), .B(B_3_0[1]), .Cin(main_4_cout), .S(S_3_0[1]), .Cout(main_3_cout));
  fulladder_main main_4 (.A(A_3_0[0]), .B(B_3_0[0]), .Cin(Cin), .S(S_3_0[0]), .Cout(main_4_cout));
endmodule
