// Logisim project comp4bit.circ as structural Verilog: 1 circuit, main circuit main
module main (
  input  [3:0] A_3_0,
  input  [3:0] B_3_0,
  output EQ,
  output GT,
  output LT
);

  wire and_1_out, and_2_out, and_3_out, and_4_out, and_5_out, and_6_out, and_7_out, and_8_out, main_1_eq,
       main_1_gt, main_1_lt, main_2_eq, main_2_gt, main_2_lt, main_3_eq, main_3_gt, main_3_lt, main_4_eq,
       main_4_gt, main_4_lt;

  comp1bit_main main_1 (.A(A_3_0[3]), .B(B_3_0[3]), .LT(main_1_lt), .EQ(main_1_eq), .GT(main_1_gt));
  comp1bit_main main_2 (.A(A_3_0[2]), .B(B_3_0[2]), .LT(main_2_lt), .EQ(main_2_eq), .GT(main_2_gt));
  and and_1 (and_1_out, main_2_eq, main_1_eq);
  and and_2 (and_2_out, main_1_eq, main_2_gt);
  and and_3 (and_3_out, main_2_lt, main_1_eq);
  comp1bit_main main_3 (.A(A_3_0[1]), .B(B_3_0[1]), .LT(main_3_lt), .EQ(main_3_eq), .GT(main_3_gt));
  and and_4 (and_4_out, and_1_out, main_3_eq);
  and and_5 (and_5_out, and_1_out, main_3_gt);
  and and_6 (and_6_out, and_1_out, main_3_lt);
  comp1bit_main main_4 (.A(A_3_0[0]), .B(B_3_0[0]), .LT(main_4_lt), .EQ(main_4_eq), .GT(main_4_gt));
  and and_7 (and_7_out, and_4_out, main_4_gt);
  and and_8 (and_8_out, main_4_lt, and_4_out);
  and and_9 (EQ, main_4_eq, and_4_out);
  or or_1 (GT, main_1_gt, and_2_out, and_5_out, and_7_out);
  or or_2 (LT, main_1_lt, and_3_out, and_6_out, and_8_out);
endmodule
