// Logisim project 0-63counter.circ as structural Verilog: 1 circuit, main circuit main
module main (
  input  [5:0] Dout
);

  wire and_1_out, and_2_out, and_3_out, and_4_out, clock_1_out;

  Clock clock_1 (.out(clock_1_out));
  T_Flip_Flop t_ff_1 (.clk(clock_1_out), .T(1'b1), .Q(Dout[0]));  // open: Qn, preset, reset, en
  T_Flip_Flop t_ff_2 (.clk(clock_1_out), .T(Dout[0]), .Q(Dout[1]));  // open: Qn, preset, reset, en
  and and_1 (and_1_out, Dout[1], Dout[0]);
  T_Flip_Flop t_ff_3 (.clk(clock_1_out), .T(and_1_out), .Q(Dout[2]));  // open: Qn, preset, reset, en
  T_Flip_Flop t_ff_4 (.clk(clock_1_out), .T(and_2_out), .Q(Dout[3]));  // open: Qn, preset, reset, en
  and and_2 (and_2_out, Dout[2], and_1_out);
  and and_3 (and_3_out, Dout[3], and_2_out);
  T_Flip_Flop t_ff_5 (.clk(clock_1_out), .T(and_3_out), .Q(Dout[4]));  // open: Qn, preset, reset, en
  and and_4 (and_4_out, Dout[4], and_3_out);
  T_Flip_Flop t_ff_6 (.clk(clock_1_out), .T(and_4_out), .Q(Dout[5]));  // open: Qn, preset, reset, en
  // Probe on Dout
endmodule
