// Logisim project Dflipflop.circ as structural Verilog: 1 circuit, main circuit main
module main (
  input  D,
  input  CP,
  output D_2
);

  wire d_ff_1_q, not_1_out, not_2_out;

  not not_1 (not_1_out, CP);
  D_Flip_Flop d_ff_1 (.clk(D), .D(not_1_out), .Q(d_ff_1_q));  // open: Qn, preset, en, reset
  not not_2 (not_2_out, not_1_out);
  D_Flip_Flop d_ff_2 (.clk(d_ff_1_q), .D(not_2_out), .Q(D_2));  // open: Qn, preset, en, reset
endmodule
