// Logisim project Dlatch.circ as structural Verilog: 1 circuit, main circuit main
module main (
  input  D,
  input  CP,
  output Q
);

  wire and_1_out, and_2_out, nor_1_out, not_1_out;

  not not_1 (not_1_out, D);
  and and_1 (and_1_out, not_1_out, CP);
  and and_2 (and_2_out, CP, D);
  nor nor_1 (nor_1_out, Q, and_2_out);
  nor nor_2 (Q, and_1_out, nor_1_out);
endmodule
