// Logisim project shiftregister.circ as structural Verilog: 1 circuit, main circuit main
module main (
  input  Shift_in,
  input  [1:0] Width,
  output [7:0] Data_out,
  output Shift_out
);

  wire clock_1_out, multiplexer_1_out, multiplexer_2_out, multiplexer_3_out, multiplexer_4_out,
       multiplexer_5_out, multiplexer_6_out, multiplexer_7_out, multiplexer_8_out;

  Clock clock_1 (.out(clock_1_out));
  D_Flip_Flop d_ff_1 (.clk(clock_1_out), .D(multiplexer_1_out), .Q(Data_out[0]));  // open: Qn, preset, en, reset
  Multiplexer #(.select(2)) multiplexer_1 (
    .in0(Data_out[0]), .in1(Shift_in), .in2(1'b0), .in3(1'b0), .out(multiplexer_1_out), .sel(Width));  // open: en
  Multiplexer #(.select(2)) multiplexer_2 (
    .in0(Data_out[1]), .in1(Data_out[0]), .in2(Shift_in), .in3(1'b0), .out(multiplexer_2_out), .sel(Width));  // open: en
  D_Flip_Flop d_ff_2 (.clk(clock_1_out), .D(multiplexer_2_out), .Q(Data_out[1]));  // open: Qn, preset, en, reset
  Multiplexer #(.select(2)) multiplexer_3 (
    .in0(Data_out[2]), .in1(Data_out[1]), .in2(Data_out[0]), .in3(Shift_in), .out(multiplexer_3_out),
    .sel(Width));  // open: en
  D_Flip_Flop d_ff_3 (.clk(clock_1_out), .D(multiplexer_3_out), .Q(Data_out[2]));  // open: Qn, preset, en, reset
  Multiplexer #(.select(2)) multiplexer_4 (
    .in0(Data_out[3]), .in1(Data_out[2]), .in2(Data_out[1]), .in3(Data_out[0]), .out(multiplexer_4_out),
    .sel(Width));  // open: en
  D_Flip_Flop d_ff_4 (.clk(clock_1_out), .D(multiplexer_4_out), .Q(Data_out[3]));  // open: Qn, preset, en, reset
  Multiplexer #(.select(2)) multiplexer_5 (
    .in0(Data_out[4]), .in1(Data_out[3]), .in2(Data_out[2]), .in3(Data_out[1]), .out(multiplexer_5_out),
    .sel(Width));  // open: en
  D_Flip_Flop d_ff_5 (.clk(clock_1_out), .D(multiplexer_5_out), .Q(Data_out[4]));  // open: Qn, preset, en, reset
  D_Flip_Flop d_ff_6 (.clk(clock_1_out), .D(multiplexer_6_out), .Q(Data_out[5]));  // open: Qn, preset, en, reset
  Multiplexer #(.select(2)) multiplexer_6 (
    .in0(Data_out[5]), .in1(Data_out[4]), .in2(Data_out[3]), .in3(Data_out[2]), .out(multiplexer_6_out),
    .sel(Width));  // open: en
  Multiplexer #(.select(2)) multiplexer_7 (
    .in0(Data_out[6]), .in1(Data_out[5]), .in2(Data_out[4]), .in3(Data_out[3]), .out(multiplexer_7_out),
    .sel(Width));  // open: en
  D_Flip_Flop d_ff_7 (.clk(clock_1_out), .D(multiplexer_7_out), .Q(Data_out[6]));  // open: Qn, preset, en, reset
  Multiplexer #(.select(2)) multiplexer_8 (
    .in0(Data_out[7]), .in1(Data_out[6]), .in2(Data_out[5]), .in3(Data_out[4]), .out(multiplexer_8_out),
    .sel(Width));  // open: en
  D_Flip_Flop d_ff_8 (.clk(clock_1_out), .D(multiplexer_8_out), .Q(Data_out[7]));  // open: Qn, preset, en, reset

  assign Shift_out = Data_out[7];
endmodule
